// Logisim project Plexers.circ as structural Verilog: 5 circuits, main circuit mux
module mux (
  input  Input1,
  input  Input2,
  input  Control,
  input  Enable,
  output Output1
);

  Multiplexer multiplexer_1 (.in0(Input1), .in1(Input2), .out(Output1), .sel(Control), .en(Enable));
endmodule

module demux (
  input  Input1,
  input  Enable,
  input  Control,
  output Output1,
  output out_5
);

  Demultiplexer demultiplexer_1 (.out0(Output1), .out1(out_5), .in(Input1), .sel(Control), .en(Enable));
endmodule

module decod (
  input  Enable,
  input  Select,
  output Output1,
  output Output2
);

  Decoder decoder_1 (.out0(Output1), .out1(Output2), .sel(Select), .en(Enable));
  // NOT_Gate not_1 is placed but not wired
endmodule

module encod (
);

  Priority_Encoder priority_encoder_1 ();  // open: in0, in1, in2, in3, in4, in5, in6, in7, out, en_in, gs, en_out
endmodule

module bselect (
  input  [7:0] Input1,
  input  [1:0] Select,
  output [2:0] Outpu1
);

  BitSelector #(.group(3)) bitselector_1 (.in(Input1), .out(Outpu1), .sel(Select));
endmodule
